# Fritzing sketch PIR (saved by Fritzing 0.9.3b)
breadboards: 1

parts:
  Componente1 = Arduino Uno (Rev3)
  R1 = Resistor [tolerance=±5% resistance=220 package=THT]
  LED1 = LED - 5mm [color="Red (633nm)" package="5 mm [THT]"]
  PIR1 = PIR sensor

nets:
  N1: Componente1.D12/MISO, R1.Pin_1
  N2: Componente1.D3_PWM, PIR1.SIG
  5V: Componente1.5V, PIR1.VDD
  GND: Componente1.GND, LED1.anode, PIR1.GND
  N3: R1.Pin_0, LED1.cathode
